# Fritzing sketch leds (saved by Fritzing 0.7.12b)
breadboards: 1

parts:
  ATtiny = attiny85 [package=dip]
  arduino_power_supply = Arduino
  R1 = 220 Ω Resistor [package=THT]
  LED2 = smd LED [color="Red (633nm)" package="0805 [SMD]"]
  R2 = 220 Ω Resistor [package=THT]
  LED1 = smd LED [color="Red (633nm)" package="0805 [SMD]"]

nets:
  N1: ATtiny.Pin_4, arduino_power_supply.GND, LED2.cathode, LED1.cathode
  N2: ATtiny.Pin_5, R2.Pin_1
  N3: ATtiny.Pin_6, R1.Pin_1
  N4: ATtiny.Pin_8, arduino_power_supply.+5V
