# Fritzing sketch attiny-arduino-softserial (saved by Fritzing 0.7.12b)
breadboards: 1

parts:
  ATtiny = attiny85 [package=dip]
  Arduino_as_Serial_Fwd = Arduino

nets:
  N1: ATtiny.Pin_4, Arduino_as_Serial_Fwd.GND
  N2: ATtiny.Pin_6, Arduino_as_Serial_Fwd.D10
  N3: ATtiny.Pin_8, Arduino_as_Serial_Fwd.+5V
